# Fritzing sketch EveBain1.2.1 (saved by Fritzing 0.9.2b)
circuit board: 2.66707cm x 7.75758cm
breadboards: 1

parts:
  3_3V = Voltage Regulator - 3.3V [package="TO220 [THT]"]
  +_- = female pin header, 2 pins [form="♀ (female)"]
  WIFI = prefix0000THISPARRRT [form="♀ (female)"]
  PRGM = female pin header, 2 pins [form="♀ (female)"]
  TX = female pin header, 2 pins [form="♀ (female)"]
  RX = female pin header, 2 pins [form="♀ (female)"]
  Nano = Arduino Nano (Rev3.0)
  GPIO = double row female pin header, 26 pins [form="♀ (female)"]

nets:
  N1: 3_3V.input_voltage, +_-.pin1, WIFI.connector7, PRGM.pin2, Nano.GND, GPIO.pin13, GPIO.pin14
  N2: 3_3V.GND, WIFI.connector1, WIFI.connector3
  N3: 3_3V.output_voltage, Nano.5V, GPIO.pin15
  N4: +_-.pin2, Nano.VIN
  N5: WIFI.connector0, RX.pin2
  N6: WIFI.connector2, Nano.RESET
  N7: WIFI.connector4, TX.pin2
  N8: WIFI.connector5, PRGM.pin1
  N9: WIFI.connector6, GPIO.pin1
  N10: TX.pin1, Nano.D1/TX
  N11: RX.pin1, Nano.D0/RX
  N12: Nano.D2, GPIO.pin12
  N13: Nano.D3, GPIO.pin11
  N14: Nano.D4, GPIO.pin10
  N15: Nano.D5, GPIO.pin9
  N16: Nano.D6, GPIO.pin8
  N17: Nano.D7, GPIO.pin7
  N18: Nano.D8, GPIO.pin6
  N19: Nano.D9, GPIO.pin5
  N20: Nano.D10, GPIO.pin4
  N21: Nano.D11/MOSI, GPIO.pin3
  N22: Nano.D12/MISO, GPIO.pin2
  N23: Nano.A7, GPIO.pin16
  N24: Nano.A6, GPIO.pin17
  N25: Nano.A5, GPIO.pin18
  N26: Nano.A4, GPIO.pin19
  N27: Nano.A3, GPIO.pin20
  N28: Nano.A2, GPIO.pin21
  N29: Nano.A1, GPIO.pin22
  N30: Nano.A0, GPIO.pin23
  N31: Nano.AREF, GPIO.pin24
  N32: Nano.3V3, GPIO.pin25
  N33: Nano.D13/SCK, GPIO.pin26

notes:
  EveBrain 1.1.1
