# Fritzing sketch EveBain1.2 (saved by Fritzing 0.9.2b)
circuit board: 4.1481cm x 5.7868cm
breadboards: 1

parts:
  3_3V = Voltage Regulator - 3.3V [package="TO220 [THT]"]  # not connected
  PWR = female pin header, 2 pins [form="♀ (female)"]
  GPIO = Generic double row female header - 26 pins [form="♀ (female)" package=THT]
  PRGM = female pin header, 2 pins [form="♀ (female)"]  # not connected
  TX = female pin header, 2 pins [form="♀ (female)"]
  RX = female pin header, 2 pins [form="♀ (female)"]
  Nano = Arduino Nano (Rev3.0)

nets:
  N1: PWR.pin1, GPIO.21, Nano.GND
  N2: PWR.pin2, Nano.VIN
  N3: GPIO.3.3V#0, Nano.A7
  N4: GPIO.SDA, Nano.A6
  N5: GPIO.SCL, Nano.A4
  N6: GPIO.04, Nano.A2
  N7: GPIO.GND#4, Nano.A0
  N8: GPIO.17, Nano.3V3
  N9: GPIO.22, Nano.D3
  N10: GPIO.3.3V#8, Nano.D5
  N11: GPIO.MOSI, Nano.D7
  N12: GPIO.MISO, Nano.D9
  N13: GPIO.SCLK, Nano.D11/MOSI
  N14: GPIO.CEO, Nano.D12/MISO
  N15: GPIO.25, Nano.D10
  N16: GPIO.GND#16, Nano.D8
  N17: GPIO.24, Nano.D6
  N18: GPIO.23, Nano.D4
  N19: GPIO.GND#19, Nano.D2
  N20: GPIO.18, Nano.D13/SCK
  N21: GPIO.RX, Nano.AREF
  N22: GPIO.TX, Nano.A1
  N23: GPIO.GND#23, Nano.A3
  N24: GPIO.5v, Nano.A5
  5V: GPIO.5V, Nano.5V
  N25: TX.pin2, Nano.D1/TX
  N26: RX.pin2, Nano.D0/RX

notes:
  EveBrain 1.1.1

custom parts:
  Generic double row female header - 26 pins: Generic double row female header
