# Fritzing sketch EveBot1.1 (saved by Fritzing 0.9.2b)
circuit board: 4.19393cm x 2.67075cm
breadboards: 1

parts:
  +_- = female pin header, 2 pins [form="♀ (female)"]
  Motor_Driver0 = female pin header, 6 pins [form="♀ (female)"]
  Motor_Driver1 = female pin header, 6 pins [form="♀ (female)"]
  A1 = female pin header, 3 pins [form="♀ (female)"]
  A0 = female pin header, 3 pins [form="♀ (female)"]
  Sonic = female pin header, 4 pins [form="♀ (female)"]
  EveBrain = Generic double row female header - 26 pins [form="♀ (female)" package=THT]

nets:
  N1: +_-.pin1, Motor_Driver0.pin1, Motor_Driver1.pin1, A1.pin2, A0.pin2, Sonic.pin4, EveBrain.GND
  N2: +_-.pin2, Motor_Driver0.pin2, Motor_Driver1.pin2, Sonic.pin1, EveBrain.5V
  N3: Motor_Driver0.pin3, EveBrain.23
  N4: Motor_Driver0.pin4, EveBrain.22
  N5: Motor_Driver0.pin5, EveBrain.SCL
  N6: Motor_Driver0.pin6, EveBrain.SDA
  N7: Motor_Driver1.pin3, EveBrain.MOSI
  N8: Motor_Driver1.pin4, EveBrain.CE1
  N9: Motor_Driver1.pin5, EveBrain.CEO
  N10: Motor_Driver1.pin6, EveBrain.24
  N11: A1.pin1, EveBrain.17
  N12: A1.pin3, A0.pin3, EveBrain.3.3V
  N13: A0.pin1, EveBrain.04
  N14: Sonic.pin2, EveBrain.MISO
  N15: Sonic.pin3, EveBrain.SCLK

notes:
  EveBot 1.1
  2.3.4.5
  6.7.8.11

custom parts:
  Generic double row female header - 26 pins: Generic double row female header
